# Fritzing sketch EMS_1 (saved by Fritzing 0.7.10b)
breadboards: 1

parts:
  U1 = 555 Timer [package="SO8 [SMD]"]
  R2/1_8KΩ = Resistor [tolerance=±5% resistance=1.8 package=THT]
  C1/100nF = Electrolytic Capacitor [capacitance=100nF package="0605 [SMD, electrolytic]"]
  C2/0_01uF = Electrolytic Capacitor [capacitance=0.1µF package="1010 [SMD, electrolytic]"]
  T1/BC327 = PNP-Transistor [package="SOT-23 [SMD]"]
  VR1/4_7KΩ = Rotary Potentiometer (Small) [maximum_resistance=4.7k]
  R1/180KΩ = Resistor [tolerance=±5% resistance=180k package=THT]
  T2/BC327 = PNP-Transistor [package="SOT-23 [SMD]"]
  R4/100Ω = Resistor [tolerance=±5% resistance=100 package=THT]
  D1 = Rectifier Diode [package=THT]
  R3/2_2KΩ = Resistor [tolerance=±5% resistance=2.2k package=THT]
  LED1 = red smd LED [package="1206 [SMD]"]
  T2 = Transformer [part_number=TY-146P package="Through Hole"]
  ELECTRODES = 2.1mm Barrel Jack with Terminal Block
  VCC/3V = Battery
  S1/ON-OFF = Reed switch [package=THT]

nets:
  GND: U1.Pin_1, C1/100nF.-, C2/0_01uF.-, T1/BC327.1, LED1.cathode, T2.2
  N1: U1.Pin_2, U1.Pin_6, R2/1_8KΩ.Pin_1, C1/100nF.+
  N2: U1.Pin_3, T1/BC327.0
  N3: U1.Pin_4, U1.Pin_8, VR1/4_7KΩ.leg2, R1/180KΩ.Pin_0, T2/BC327.2, D1.cathode, S1/ON-OFF.pin_1
  N4: U1.Pin_5, C2/0_01uF.+
  N5: R2/1_8KΩ.Pin_0, R1/180KΩ.Pin_1
  N6: T1/BC327.2, R3/2_2KΩ.Pin_1
  N7: VR1/4_7KΩ.leg1, R3/2_2KΩ.Pin_0
  N8: VR1/4_7KΩ.wiper, T2/BC327.0
  N9: T2/BC327.1, R4/100Ω.Pin_0, D1.anode, T2.1
  N10: R4/100Ω.Pin_1, LED1.anode
  N11: T2.4, ELECTRODES.POS
  N12: T2.5, ELECTRODES.NEG, VCC/3V.-
  N13: VCC/3V.+, S1/ON-OFF.pin_2

notes:
  We actually use the 7555 (which is retro-compatible with classic 555)
  basically a 1.8K resistor

custom parts:
  Transformer: A Triad Magnetics 600Ohm:600Ohm audio transformer.
