# Fritzing sketch EMS_1_breadboard (saved by Fritzing 0.7.10b)
breadboards: 1

parts:
  U1 = 555 Timer [package="SO8 [SMD]"]
  VCC1 = Battery  # not connected
  R1 = Resistor [tolerance=±5% resistance=180k package=THT]

nets:
  N1: U1.Pin_6, R1.Pin_1
  N2: U1.Pin_7, R1.Pin_0
